// Logisim project Dragon_5.circ as structural Verilog: 5 circuits, main circuit main
module main (
);

  Pipeline_ID ID_Stage ();  // open: Inst_Cache_1_IN, Inst_Cache_2_IN, WE, Inst_1_out, Inst_2_out
  Register_File reg_file ();  // open: RegF_rst, RegF_WE, RegF_A1, RegF_A2, RegF_A3, RegF_WD, RegF_D1, RegF_D2
  ALU Arithmetic_logic_Unit ();  // open: ALU_OP_IN, ALU_A_IN, ALU_B_IN, ALU_FLAG_IN, ALU_RES_OUT, ALU_FLAG_OUT
endmodule

module ALU (
  input  [3:0] ALU_OP_IN,
  input  [15:0] ALU_A_IN,
  input  [15:0] ALU_B_IN,
  input  [15:0] ALU_FLAG_IN,
  output [15:0] ALU_RES_OUT,
  output [15:0] ALU_FLAG_OUT
);

  wire adder_1_cout, adder_2_cout, adder_3_cout;
  wire [15:0] adder_1_out;

  Pull_Resistor pull_resistor_1 (.node(ALU_RES_OUT));
  Adder #(.width(4)) adder_1 (
    .a(ALU_A_IN[3:0]), .b(ALU_B_IN[3:0]), .out(adder_1_out[3:0]), .cout(adder_1_cout));  // open: cin
  Adder #(.width(4)) adder_2 (
    .a(ALU_A_IN[7:4]), .b(ALU_B_IN[7:4]), .out(adder_1_out[7:4]), .cin(adder_1_cout), .cout(adder_2_cout));
  Adder #(.width(4)) adder_3 (
    .a(ALU_A_IN[11:8]), .b(ALU_B_IN[11:8]), .out(adder_1_out[11:8]), .cin(adder_2_cout), .cout(adder_3_cout));
  Adder #(.width(4)) adder_4 (
    .a(ALU_A_IN[15:12]), .b(ALU_B_IN[15:12]), .out(adder_1_out[15:12]), .cin(adder_3_cout));  // open: cout
  Controlled_Buffer #(.width(16)) controlled_buffer_1 (.in(adder_1_out));  // open: out, en

  // Other names for the same wires on the sheet: ALU_A[15:0] = ALU_A_IN; ALU_B[15:0] = ALU_B_IN;
  //   ALU_OP[3:0] = ALU_OP_IN; ALU_RES[15:0] = ALU_RES_OUT
endmodule

module Register_File (
  input  RegF_rst,
  input  RegF_WE,
  input  [4:0] RegF_A1,
  input  [4:0] RegF_A2,
  input  [4:0] RegF_A3,
  input  [15:0] RegF_WD,
  output [15:0] RegF_D1,
  output [15:0] RegF_D2
);

  wire clock_1_out;
  wire [4:0] multiplexer_1_out, multiplexer_2_out;
  wire [15:0] bit_extender_1_out, bit_extender_2_out;

  assign bit_extender_1_out = {{11{1'b0}}, multiplexer_1_out};  // Bit_Extender bit_extender_1
  Multiplexer #(.width(5)) multiplexer_1 (.in0(RegF_A1), .in1(RegF_A3), .out(multiplexer_1_out), .sel(RegF_WE));
  Clock clock_1 (.out(clock_1_out));
  assign bit_extender_2_out = {{11{1'b0}}, multiplexer_2_out};  // Bit_Extender bit_extender_2
  Multiplexer #(.width(5)) multiplexer_2 (.in0(RegF_A2), .in1(RegF_A3), .out(multiplexer_2_out), .sel(RegF_WE));
  RAM #(.addrWidth(16), .dataWidth(16)) ram_1 (
    .addr(bit_extender_1_out), .we(RegF_WE), .oe(1'b1), .clk(clock_1_out), .din(RegF_WD), .dout(RegF_D1));
  RAM #(.addrWidth(16), .dataWidth(16)) ram_2 (
    .addr(bit_extender_2_out), .we(RegF_WE), .oe(1'b1), .clk(clock_1_out), .din(RegF_WD), .dout(RegF_D2));

  // Other names for the same wires on the sheet: RegF_bus_A[15:0] = RegF_D1; RegF_bus_B[15:0] = RegF_D2;
  //   RegF_D_in[15:0] = RegF_WD; RegF_reset = RegF_rst
endmodule

module Pipeline_ID (
  input  WE,
  input  [15:0] Inst_Cache_1_IN,
  input  [15:0] Inst_Cache_2_IN,
  output [15:0] Inst_1_out,
  output [15:0] Inst_2_out
);

  wire reset, undriven;

  Register #(.width(16)) register_1 (.D(Inst_Cache_1_IN), .en(undriven), .clk(WE), .Q(Inst_1_out), .clr(reset));
  Clock clock_1 (.out(WE));
  Register #(.width(16)) register_2 (.D(Inst_Cache_2_IN), .en(undriven), .clk(WE), .Q(Inst_2_out), .clr(reset));
endmodule

module Instruction_Cache (
  input  [15:0] InstC_A,
  input  [15:0] InstC_MBR,
  input  InstC_WE,
  input  InstC_CU_Acc,
  output [19:0] InstC_RAM_A_BUS,
  output [15:0] InstC_Data_Out,
  output InstC_CU_Stall_Req
);

  wire and_1_out, clock_1_out, comparator_1_eq, undriven, undriven_2;
  wire [15:0] intr_cache_tag_sram_dout;
  wire [15:15] or_1_out;

  buf or_1 (or_1_out[15], undriven);  // OR_Gate
  Clock clock_1 (.out(clock_1_out));
  RAM #(.addrWidth(16), .dataWidth(16)) istr_cache_data_sram (
    .addr(InstC_A), .we(undriven), .oe(undriven_2), .clk(clock_1_out), .dout(InstC_Data_Out));  // open: din
  RAM #(.addrWidth(16), .dataWidth(16)) intr_cache_tag_sram (
    .addr(InstC_A), .we(undriven), .oe(1'b1), .clk(clock_1_out), .din({or_1_out[15], InstC_MBR[14:0]}),
    .dout(intr_cache_tag_sram_dout));
  Comparator #(.mode("unsigned"), .width(15)) comparator_1 (
    .a(intr_cache_tag_sram_dout[14:0]), .b(InstC_MBR[14:0]), .eq(comparator_1_eq));  // open: gt, lt
  and and_1 (and_1_out, comparator_1_eq, intr_cache_tag_sram_dout[15]);

  // Notes on the sheet:
  //   tag
  //   valid bit
  //   index + offset
  //   data
  //   tag + meta data
  //   15-bit tag | 1 valid bit
  //   valid
  //   tag
  //   Cache Hit
endmodule
